# Fritzing sketch Wiring (saved by Fritzing 0.9.3b)

parts:
  UNO = Arduino Uno (Rev3)
  StartButton = Pushbutton [package="[SMD]"]
  WireLoop = Pushbutton [package="[SMD]"]
  LCD = LCM1602 IIC [part_number="LCM1602 IIC" chip_label="LCM1602 IIC" package="DIP (Dual Inline) [THT]"]
  Buzzer = Piezo Speaker  # not connected
  RedLed = smd LED [color="Red (633nm)" package="0603 [SMD]"]
  GreenLed = smd LED [color="Red (633nm)" package="0603 [SMD]"]
  OverButton = Pushbutton [package="[SMD]"]

nets:
  N1: UNO.A4/SDA, LCD.SDA
  N2: UNO.A5/SCL, LCD.SCL
  N3: UNO.D9_PWM, OverButton.Pin_3, OverButton.Pin_4
  GND: UNO.GND, StartButton.Pin_1, StartButton.Pin_2, WireLoop.Pin_1, WireLoop.Pin_2, LCD.GND, RedLed.cathode, GreenLed.cathode, OverButton.Pin_2
  N4: UNO.D2, RedLed.anode
  N5: UNO.D3_PWM, GreenLed.anode
  N6: UNO.D6_PWM, StartButton.Pin_3, StartButton.Pin_4
  N7: UNO.D7, WireLoop.Pin_3, WireLoop.Pin_4
  5V: UNO.5V, LCD.VCC

custom parts:
  LCM1602 IIC: I2C-Module to use a 1602 or 2004 LCD on with the wire.h libory Serial LCD Modul

// code stored in the sketch: cpe23osz.ino
#include <Wire.h>
#include <LiquidCrystal_I2C.h>

LiquidCrystal_I2C lcd(0x3F, 16, 2);  // Change the address (0x27) to your LCD address

const int loopPin = 7;          // Digital pin for the loop wire
const int buzzerPin = 8;        // Digital pin for the buzzer
const int startButtonPin = 6;   // Digital pin for the start button
const int overButtonPin = 9;
const unsigned long gameTime = 120000;  // 120 seconds (2 minutes) in milliseconds
const int rledPin = 2;
const int gledPin = 3;

unsigned long gameStartTime;
unsigned long lastTime;
bool gameRunning = false;
unsigned long elapsedTime = 0;
int loopCount = 0;

void setup() {
  pinMode(loopPin, INPUT_PULLUP);       // Set loopPin as input with pull-up resistor
  pinMode(buzzerPin, OUTPUT);
  pinMode(startButtonPin, INPUT_PULLUP); // Set startButtonPin as input with pull-up resistor
  pinMode(overButtonPin, INPUT_PULLUP);
  pinMode(rledPin, OUTPUT);
  pinMode(gledPin, OUTPUT);
  
  lcd.init();
  lcd.backlight();
  lcd.setCursor(0, 0);
  lcd.print("Vonal Vezeto");
  delay(2000);
  lcd.clear();
}

void loop() {
  if (!gameRunning) {
    lcd.setCursor(0, 0);
    
    lcd.print("Emeld fel a palc");
    lcd.setCursor(0, 1);
    lcd.print("at a kezdehez!");

    if (digitalRead(startButtonPin) == HIGH) {
      lcd.clear();
      lcd.setCursor(0, 0);
      lcd.print("Jatek inditva!");
      digitalWrite(gledPin, HIGH);
      delay(1000);
      digitalWrite(gledPin, LOW);
      lcd.clear();
      startGame(); // Start the game when the button is pressed
    }
  } else {
    unsigned long currentTime = millis();
    elapsedTime = currentTime - gameStartTime;
    
    if (elapsedTime >= gameTime) {
      endGame();
    }
    if (digitalRead(overButtonPin) == LOW){
      endGame();
    }
    

    lcd.setCursor(0, 0);
    lcd.print("Ido: ");
    lcd.print((gameTime - elapsedTime) / 1000);  // Display remaining time in seconds
    lcd.print("s ");
    
    lcd.setCursor(0, 1);
    lcd.print("Vezesd a hurkot! ");
    lcd.print("Szamlalo: ");
    lcd.print(loopCount);

    if (digitalRead(loopPin) == LOW) {
      loopCount++;
      lcd.clear();
      digitalWrite(rledPin, HIGH);
      digitalWrite(buzzerPin, HIGH);
      lcd.setCursor(0, 0);
      lcd.print("Hozzaertel!");
      lcd.setCursor(0, 1);
      lcd.print("Szamlalo: ");
      lcd.print(loopCount);
      delay(1000);
      digitalWrite(rledPin, LOW);
      digitalWrite(buzzerPin, LOW);
      lcd.clear();
    }
  }
}

void startGame() {
  gameStartTime = millis();  // Record the start time
  gameRunning = true;
  loopCount = 0;
}

void endGame() {
  gameRunning = false;
  lcd.clear();
  lcd.setCursor(0, 0);
  lcd.print("Jatek vege!");
  lcd.setCursor(0, 1);
  lcd.print("Szamlalo: ");
  lcd.print(loopCount);
  digitalWrite(buzzerPin, HIGH);  // Turn on the buzzer
  digitalWrite(rledPin, HIGH);
  delay(1000);
  digitalWrite(buzzerPin, LOW);   // Turn off the buzzer
  digitalWrite(rledPin, LOW);
  delay(5000);
  lcd.clear();
  lcd.print("Tedd vissza a ");
  lcd.setCursor(0, 1);
  lcd.print("kezdeshez!");

  // Wait until the start button is pressed to clear the display
  while (digitalRead(startButtonPin) == HIGH) {
    delay(100);
    }
  lcd.clear();
}
